// Logisim project 15：52版.circ as structural Verilog: 9 circuits, main circuit main
module main (
  input  in_1,
  output [31:0] out_2,
  output [31:0] out_3,
  output out_4,
  output [4:0] out_5,
  output [31:0] out_6,
  output out_7,
  output [31:0] out_8,
  output [31:0] out_9
);

  wire ALUSrc, Branch, clk, equal, EXTsign;
  wire [2:0] ALUOp, DMOp, MemtoReg, NPCOp, RegDst;
  wire [31:0] imm32, multiplexer_3_out, NPC, PC_4, RD, RD1;

  Clock clock_1 (.out(clk));
  Multiplexer #(.select(3), .width(5), .enable("false")) multiplexer_1 (
    .in0(out_2[20:16]), .in1(out_2[15:11]), .in2({5{1'b1}}), .out(out_5), .sel(RegDst));  // open: in3, in4, in5, in6, in7
  Multiplexer #(.select(3), .width(32), .enable("false")) multiplexer_2 (
    .in0(out_8), .in1(RD), .in2(PC_4), .out(out_6), .sel(MemtoReg));  // open: in3, in4, in5, in6, in7
  NPC npc_1 (
    .in_2(equal), .in_3(Branch), .in_4(imm32), .out_8(NPC), .in_1(out_3), .out_9(PC_4), .in_5(out_2[25:0]),
    .in_6(RD1), .in_7(NPCOp));
  // Probe on out_2
  GRF grf_1 (
    .in_4(out_2[25:21]), .in_5(out_2[20:16]), .in_6(out_5), .in_7(out_6), .out_8(RD1), .out_9(out_9),
    .in_1(clk), .in_2(in_1), .in_3(out_4));
  PC pc_1 (.in_1(clk), .in_2(in_1), .in_3(NPC), .out_4(out_3));
  Multiplexer #(.width(32), .enable("false")) multiplexer_3 (
    .in0(out_9), .in1(imm32), .out(multiplexer_3_out), .sel(ALUSrc));
  IFU ifu_1 (.in_1(out_3), .out_2(out_2));
  ALU alu_1 (.in_2(RD1), .in_3(multiplexer_3_out), .out_4(equal), .out_5(out_8), .in_1(ALUOp));
  EXT ext_1 (.in_1(out_2[15:0]), .out_3(imm32), .in_2(EXTsign));
  Controller controller_1 (
    .Branch(Branch), .ALUCtrl(ALUOp), .Func(out_2[5:0]), .Op(out_2[31:26]), .DMOp(DMOp), .NPCOp(NPCOp),
    .MemToReg(MemtoReg), .ALUSrc(ALUSrc), .EXTsign(EXTsign), .Mem_Write(out_7), .RegWrite(out_4),
    .RegDst(RegDst));
  DM dm_1 (.in_4(out_8), .in_5(out_9), .out_7(RD), .in_1(out_7), .in_2(clk), .in_3(in_1), .in_6(DMOp));

  // Other names for the same wires on the sheet: funcode[5:0] = out_2[5:0]; imm[15:0] = out_2[15:0];
  //   index[25:0] = out_2[25:0]; Instr[31:0] = out_2; rd_t[4:0] = out_2[15:11]; rt[4:0] = out_2[20:16];
  //   rs_t[4:0] = out_2[25:21]; opcode[5:0] = out_2[31:26]; ALUresult[31:0] = out_8; MemAddr[31:0] = out_8;
  //   MemWrite = out_7; PC[31:0] = out_3; rs[31:0] = RD1; MemData[31:0] = out_9; RD2[31:0] = out_9;
  //   RegAddr[4:0] = out_5; RegData[31:0] = out_6; RegWrite = out_4; reset = in_1
endmodule

module GRF (
  input  in_1,
  input  in_2,
  input  in_3,
  input  [4:0] in_4,
  input  [4:0] in_5,
  input  [4:0] in_6,
  input  [31:0] in_7,
  output [31:0] out_8,
  output [31:0] out_9
);

  wire [31:0] in2, in3, in4, in5, in6, in7, in8, in9, in10, in11, in12, in13, in14, in15, in16, in17, in18,
       in19, in20, in21, in22, in23, in24, in25, in26, in27, in28, in29, in30, in31, in32, out1, out2, out3,
       out4, out5, out6, out7, out8, out9, out10, out11, out12, out13, out14, out15, out16, out17, out18,
       out19, out20, out21, out22, out23, out24, out25, out26, out27, out28, out29, out30, out31, out32;

  Demultiplexer #(.select(5), .width(32), .tristate("true")) demultiplexer_1 (
    .out1(in2), .out2(in3), .out3(in4), .out4(in5), .out5(in6), .out6(in7), .out7(in8), .out8(in9),
    .out9(in10), .out10(in11), .out11(in12), .out12(in13), .out13(in14), .out14(in15), .out15(in16),
    .out16(in17), .out17(in18), .out18(in19), .out19(in20), .out20(in21), .out21(in22), .out22(in23),
    .out23(in24), .out24(in25), .out25(in26), .out26(in27), .out27(in28), .out28(in29), .out29(in30),
    .out30(in31), .out31(in32), .in(in_7), .sel(in_6));  // open: out0, en
  Multiplexer #(.select(5), .width(32)) multiplexer_1 (
    .in0(out1), .in1(out2), .in2(out3), .in3(out4), .in4(out5), .in5(out6), .in6(out7), .in7(out8),
    .in8(out9), .in9(out10), .in10(out11), .in11(out12), .in12(out13), .in13(out14), .in14(out15),
    .in15(out16), .in16(out17), .in17(out18), .in18(out19), .in19(out20), .in20(out21), .in21(out22),
    .in22(out23), .in23(out24), .in24(out25), .in25(out26), .in26(out27), .in27(out28), .in28(out29),
    .in29(out30), .in30(out31), .in31(out32), .out(out_8), .sel(in_4));  // open: en
  Register #(.width(32)) register_1 (.D({32{1'b0}}), .en(in_3), .Q(out1), .clk(in_1), .clr(in_2));
  Register #(.width(32)) register_2 (.D(in9), .en(in_3), .Q(out9), .clk(in_1), .clr(in_2));
  Register #(.width(32)) register_3 (.D(in17), .en(in_3), .Q(out17), .clk(in_1), .clr(in_2));
  Register #(.width(32)) register_4 (.D(in25), .en(in_3), .Q(out25), .clk(in_1), .clr(in_2));
  Register #(.width(32)) register_5 (.D(in2), .en(in_3), .Q(out2), .clk(in_1), .clr(in_2));
  Register #(.width(32)) register_6 (.D(in10), .en(in_3), .Q(out10), .clk(in_1), .clr(in_2));
  Register #(.width(32)) register_7 (.D(in18), .en(in_3), .Q(out18), .clk(in_1), .clr(in_2));
  Register #(.width(32)) register_8 (.D(in26), .en(in_3), .Q(out26), .clk(in_1), .clr(in_2));
  Register #(.width(32)) register_9 (.D(in3), .en(in_3), .Q(out3), .clk(in_1), .clr(in_2));
  Register #(.width(32)) register_10 (.D(in11), .en(in_3), .Q(out11), .clk(in_1), .clr(in_2));
  Register #(.width(32)) register_11 (.D(in19), .en(in_3), .Q(out19), .clk(in_1), .clr(in_2));
  Register #(.width(32)) register_12 (.D(in27), .en(in_3), .Q(out27), .clk(in_1), .clr(in_2));
  Multiplexer #(.select(5), .width(32)) multiplexer_2 (
    .in0(out1), .in1(out2), .in2(out3), .in3(out4), .in4(out5), .in5(out6), .in6(out7), .in7(out8),
    .in8(out9), .in9(out10), .in10(out11), .in11(out12), .in12(out13), .in13(out14), .in14(out15),
    .in15(out16), .in16(out17), .in17(out18), .in18(out19), .in19(out20), .in20(out21), .in21(out22),
    .in22(out23), .in23(out24), .in24(out25), .in25(out26), .in26(out27), .in27(out28), .in28(out29),
    .in29(out30), .in30(out31), .in31(out32), .out(out_9), .sel(in_5));  // open: en
  Register #(.width(32)) register_13 (.D(in4), .en(in_3), .Q(out4), .clk(in_1), .clr(in_2));
  Register #(.width(32)) register_14 (.D(in12), .en(in_3), .Q(out12), .clk(in_1), .clr(in_2));
  Register #(.width(32)) register_15 (.D(in20), .en(in_3), .Q(out20), .clk(in_1), .clr(in_2));
  Register #(.width(32)) register_16 (.D(in28), .en(in_3), .Q(out28), .clk(in_1), .clr(in_2));
  Register #(.width(32)) register_17 (.D(in5), .en(in_3), .Q(out5), .clk(in_1), .clr(in_2));
  Register #(.width(32)) register_18 (.D(in13), .en(in_3), .Q(out13), .clk(in_1), .clr(in_2));
  Register #(.width(32)) register_19 (.D(in21), .en(in_3), .Q(out21), .clk(in_1), .clr(in_2));
  Register #(.width(32)) register_20 (.D(in29), .en(in_3), .Q(out29), .clk(in_1), .clr(in_2));
  Register #(.width(32)) register_21 (.D(in6), .en(in_3), .Q(out6), .clk(in_1), .clr(in_2));
  Register #(.width(32)) register_22 (.D(in14), .en(in_3), .Q(out14), .clk(in_1), .clr(in_2));
  Register #(.width(32)) register_23 (.D(in22), .en(in_3), .Q(out22), .clk(in_1), .clr(in_2));
  Register #(.width(32)) register_24 (.D(in30), .en(in_3), .Q(out30), .clk(in_1), .clr(in_2));
  Register #(.width(32)) register_25 (.D(in7), .en(in_3), .Q(out7), .clk(in_1), .clr(in_2));
  Register #(.width(32)) register_26 (.D(in15), .en(in_3), .Q(out15), .clk(in_1), .clr(in_2));
  Register #(.width(32)) register_27 (.D(in23), .en(in_3), .Q(out23), .clk(in_1), .clr(in_2));
  Register #(.width(32)) register_28 (.D(in31), .en(in_3), .Q(out31), .clk(in_1), .clr(in_2));
  Register #(.width(32)) register_29 (.D(in8), .en(in_3), .Q(out8), .clk(in_1), .clr(in_2));
  Register #(.width(32)) register_30 (.D(in16), .en(in_3), .Q(out16), .clk(in_1), .clr(in_2));
  Register #(.width(32)) register_31 (.D(in24), .en(in_3), .Q(out24), .clk(in_1), .clr(in_2));
  Register #(.width(32)) register_32 (.D(in32), .en(in_3), .Q(out32), .clk(in_1), .clr(in_2));

  // Other names for the same wires on the sheet: A1[4:0] = in_4; A2[4:0] = in_5; A3[4:0] = in_6; clk = in_1;
  //   RD1[31:0] = out_8; RD2[31:0] = out_9; reset = in_2; WD[31:0] = in_7; we = in_3
endmodule

module ALU (
  input  [2:0] in_1,
  input  [31:0] in_2,
  input  [31:0] in_3,
  output out_4,
  output [31:0] out_5
);

  wire [31:0] adder_1_out, or_1_out, shifter_1_out, subtractor_1_out;

  assign or_1_out = in_2 | in_3;  // OR_Gate or_1, 32 bits wide
  Shifter #(.width(32)) shifter_1 (.in(in_3), .\dist (5'b10000), .out(shifter_1_out));
  Subtractor #(.width(32)) subtractor_1 (.a(in_2), .b(in_3), .out(subtractor_1_out));  // open: bin, bout
  Adder #(.width(32)) adder_1 (.a(in_2), .b(in_3), .out(adder_1_out));  // open: cin, cout
  Multiplexer #(.select(3), .width(32), .enable("false")) multiplexer_1 (
    .in0(adder_1_out), .in1(subtractor_1_out), .in2(or_1_out), .in3(shifter_1_out), .out(out_5), .sel(in_1));  // open: in4, in5, in6, in7
  Comparator #(.width(32)) comparator_1 (.a({32{1'b0}}), .b(subtractor_1_out), .eq(out_4));  // open: gt, lt

  // Other names for the same wires on the sheet: ALUOp[2:0] = in_1
endmodule

module Controller (
  input  [5:0] Func,
  input  [5:0] Op,
  output [2:0] MemToReg,
  output Mem_Write,
  output Branch,
  output [2:0] ALUCtrl,
  output ALUSrc,
  output EXTsign,
  output RegWrite,
  output [2:0] RegDst,
  output [2:0] DMOp,
  output [2:0] NPCOp
);

  wire add, j, jal, jalr, jr, lb, lh, lui, lw, not_1_out, not_2_out, not_3_out, not_4_out, not_5_out,
       not_6_out, not_7_out, not_8_out, not_9_out, not_10_out, not_11_out, not_12_out, or_5_out, or_6_out,
       or_8_out, or_9_out, or_10_out, or_11_out, ori, R, sb, sh, sub, sw;

  not not_1 (not_1_out, Func[5]);
  not not_2 (not_2_out, Func[3]);
  not not_3 (not_3_out, Func[4]);
  not not_4 (not_4_out, Func[0]);
  not not_5 (not_5_out, Func[2]);
  not not_6 (not_6_out, Func[1]);
  not not_7 (not_7_out, Op[5]);
  not not_8 (not_8_out, Op[2]);
  not not_9 (not_9_out, Op[3]);
  not not_10 (not_10_out, Op[4]);
  not not_11 (not_11_out, Op[1]);
  not not_12 (not_12_out, Op[0]);
  and and_1 (ori, Op[0], not_11_out, Op[2], Op[3], not_10_out, not_7_out);
  and and_2 (lw, Op[0], Op[1], not_8_out, not_9_out, not_10_out, Op[5]);
  and and_3 (sw, Op[0], Op[1], not_8_out, Op[3], not_10_out, Op[5]);
  and and_4 (Branch, not_12_out, not_11_out, Op[2], not_9_out, not_10_out, not_7_out);
  and and_5 (R, not_12_out, not_11_out, not_8_out, not_9_out, not_10_out, not_7_out);
  and and_6 (lui, Op[0], Op[1], Op[2], Op[3], not_10_out, not_7_out);
  and and_7 (lb, not_12_out, not_11_out, not_8_out, not_9_out, not_10_out, Op[5]);
  and and_8 (lh, Op[0], not_11_out, not_8_out, not_9_out, not_10_out, Op[5]);
  and and_9 (sb, not_12_out, not_11_out, not_8_out, Op[3], not_10_out, Op[5]);
  and and_10 (sh, Op[0], not_11_out, not_8_out, Op[3], not_10_out, Op[5]);
  and and_11 (j, not_12_out, Op[1], not_8_out, not_9_out, not_10_out, not_7_out);
  and and_12 (jal, Op[0], Op[1], not_8_out, not_9_out, not_10_out, not_7_out);
  and and_13 (add, R, not_4_out, not_6_out, not_5_out, not_2_out, not_3_out, Func[5]);
  and and_14 (sub, R, not_4_out, Func[1], not_5_out, not_2_out, not_3_out, Func[5]);
  and and_15 (jalr, R, Func[0], not_6_out, not_5_out, Func[3], not_3_out, not_1_out);
  and and_16 (jr, R, not_4_out, not_6_out, not_5_out, Func[3], not_3_out, not_1_out);
  or or_1 (MemToReg[0], lw, lb, lh);
  or or_2 (MemToReg[1], jalr, jal);
  or or_3 (ALUCtrl[0], sub, lui);
  or or_4 (ALUCtrl[1], lui, ori);
  or or_5 (or_5_out, lui, ori);
  or or_6 (or_6_out, lb, sb, lw, lh, sh, sw);
  or or_7 (Mem_Write, sh, sb, sw);
  buf or_8 (or_8_out, Branch);  // OR_Gate
  or or_9 (or_9_out, lb, sb, lw, lh, sh, sw);
  or or_10 (or_10_out, lui, ori, add, sub, jalr, jr);
  or or_11 (or_11_out, lh, lb, lw);
  or or_12 (RegDst[0], add, sub, jalr);
  buf or_13 (RegDst[1], jalr);  // OR_Gate
  or or_14 (DMOp[0], lh, sh);
  or or_15 (DMOp[1], lb, sb);
  or or_16 (NPCOp[0], Branch, jr, jalr);
  or or_17 (NPCOp[1], j, jal, jalr, jr);
  or or_18 (ALUSrc, or_5_out, or_6_out);
  or or_19 (EXTsign, or_8_out, or_9_out);
  or or_20 (RegWrite, or_10_out, or_11_out);

  assign ALUCtrl[2] = 1'b0;
  assign DMOp[2] = 1'b0;
  assign MemToReg[2] = 1'b0;
  assign NPCOp[2] = 1'b0;
  assign RegDst[2] = 1'b0;

  // Other names for the same wires on the sheet: beq = Branch

  // Notes on the sheet:
  //   延长线
endmodule

module EXT (
  input  [15:0] in_1,
  input  in_2,
  output [31:0] out_3
);

  wire [31:0] bit_extender_1_out, bit_extender_2_out;

  assign bit_extender_1_out = {{16{1'b0}}, in_1};  // Bit_Extender bit_extender_1
  assign bit_extender_2_out = {{16{in_1[15]}}, in_1};  // Bit_Extender bit_extender_2
  Multiplexer #(.width(32), .enable("false")) multiplexer_1 (
    .in0(bit_extender_1_out), .in1(bit_extender_2_out), .out(out_3), .sel(in_2));
endmodule

module IFU (
  input  [31:0] in_1,
  output [31:0] out_2
);

  wire [31:0] subtractor_1_out;

  Subtractor #(.width(32)) subtractor_1 (.a(in_1), .b(32'h3000), .out(subtractor_1_out));  // open: bin, bout
  ROM #(.addrWidth(12), .dataWidth(32)) rom_1 (.addr(subtractor_1_out[13:2]), .data(out_2));  // open: sel

  // Other names for the same wires on the sheet: PC[31:0] = in_1

  // Notes on the sheet:
  //   contents of rom_1 (hex, n*v repeats v):
  //   34040001 3484007b 3405ffff 34000001 3c09ffff 3c0a007b 3c0bffff 3c00ffff 1258020 8b8820 16b9020
  //   aa6022 1456822 ab7022 1657822 12bc022 34060010 accb0004 accc0000 accdfffc ac0e0004 ac0e0000 e63822
  //   accb0014 8cc80004 8cc90000 8ccafffc 8c0b0004 8c0c0000 8ccd0014 a4c90004 a4ca0000 a4cbfffc a40d0004
  //   a40b0000 a4cc0014 84ca0004 84cb0000 84ccfffc 840f0004 840e0000 84c90014 a0ca0004 a0cb0000 a0ccfffc
  //   a00f0004 a00e0000 a0c90014 80c90004 80ca0000 80cbfffc 800d0004 800b0000 80cc0014
endmodule

module DM (
  input  in_1,
  input  in_2,
  input  in_3,
  input  [31:0] in_4,
  input  [31:0] in_5,
  input  [2:0] in_6,
  output [31:0] out_7
);

  wire [7:0] multiplexer_5_out;
  wire [15:0] multiplexer_4_out;
  wire [31:0] bit_extender_1_out, bit_extender_2_out, in, multiplexer_1_out, multiplexer_2_out, out;

  Multiplexer #(.width(32), .enable("false")) multiplexer_1 (
    .in0({out[31:16], in_5[15:0]}), .in1({in_5[15:0], out[15:0]}), .out(multiplexer_1_out), .sel(in_4[1]));
  Multiplexer #(.select(2), .width(32), .enable("false")) multiplexer_2 (
    .in0({out[31:8], in_5[7:0]}), .in1({out[31:16], in_5[7:0], out[7:0]}),
    .in2({out[31:24], in_5[7:0], out[15:0]}), .in3({in_5[7:0], out[23:0]}), .out(multiplexer_2_out),
    .sel(in_4[1:0]));
  RAM #(.addrWidth(12), .dataWidth(32), .bus("separate")) ram_1 (
    .addr(in_4[13:2]), .din(in), .data(out), .str(in_1), .clk(in_2), .clr(in_3));  // open: sel, ld
  Multiplexer #(.select(3), .width(32), .enable("false")) multiplexer_3 (
    .in0(in_5), .in1(multiplexer_1_out), .in2(multiplexer_2_out), .out(in), .sel(in_6));  // open: in3, in4, in5, in6, in7
  Multiplexer #(.width(16), .enable("false")) multiplexer_4 (
    .in0(out[15:0]), .in1(out[31:16]), .out(multiplexer_4_out), .sel(in_4[1]));
  Multiplexer #(.select(2), .width(8), .enable("false")) multiplexer_5 (
    .in0(out[7:0]), .in1(out[15:8]), .in2(out[23:16]), .in3(out[31:24]), .out(multiplexer_5_out),
    .sel(in_4[1:0]));
  assign bit_extender_1_out = {{16{multiplexer_4_out[15]}}, multiplexer_4_out};  // Bit_Extender bit_extender_1
  assign bit_extender_2_out = {{24{multiplexer_5_out[7]}}, multiplexer_5_out};  // Bit_Extender bit_extender_2
  Multiplexer #(.select(3), .width(32), .enable("false")) multiplexer_6 (
    .in0(out), .in1(bit_extender_1_out), .in2(bit_extender_2_out), .out(out_7), .sel(in_6));  // open: in3, in4, in5, in6, in7

  // Other names for the same wires on the sheet: MD_0_7[7:0] = in_5[7:0]; MemData[31:0] = in_5;
  //   MD_16_23[7:0] = in_5[23:16]; MD_24_31[7:0] = in_5[31:24]; MD_8_15[7:0] = in_5[15:8]; out_0_7[7:0] = out[7:0];
  //   out_8_15[7:0] = out[15:8]; out_16_23[7:0] = out[23:16]; out_24_31[7:0] = out[31:24]; clk = in_2;
  //   DMOp[2:0] = in_6; MemAddr[31:0] = in_4; MemWrite = in_1; RD[31:0] = out_7; reset = in_3

  // Notes on the sheet:
  //   MemAddr 就是 ALUresult
endmodule

module NPC (
  input  [31:0] in_1,
  input  in_2,
  input  in_3,
  input  [31:0] in_4,
  input  [25:0] in_5,
  input  [31:0] in_6,
  input  [2:0] in_7,
  output [31:0] out_8,
  output [31:0] out_9
);

  wire and_1_out;
  wire [31:0] adder_2_out, PCBranch, shifter_1_out;

  Shifter #(.width(32)) shifter_1 (.in(in_4), .\dist (5'b00010), .out(shifter_1_out));
  Adder #(.width(32)) adder_1 (.a(in_1), .b(32'h4), .out(out_9));  // open: cin, cout
  Adder #(.width(32)) adder_2 (.a(shifter_1_out), .b(out_9), .out(adder_2_out));  // open: cin, cout
  Multiplexer #(.width(32), .enable("false")) multiplexer_1 (
    .in0(out_9), .in1(adder_2_out), .out(PCBranch), .sel(and_1_out));
  and and_1 (and_1_out, in_2, in_3);
  Multiplexer #(.select(3), .width(32), .enable("false")) multiplexer_2 (
    .in0(out_9), .in1(PCBranch), .in2({2'b00, in_5, in_1[31:28]}), .in3(in_6), .out(out_8), .sel(in_7));  // open: in4, in5, in6, in7

  // Other names for the same wires on the sheet: Branch = in_3; equal = in_2; imm32[31:0] = in_4; NPCOp[2:0] = in_7;
  //   PC[31:0] = in_1; PC_4[31:0] = out_9; PC_prime[31:0] = out_8; PCJ_al[29:0] = {in_5, in_1[31:28]};
  //   index[25:0] = in_5; Grs[31:0] = in_6; PCJ_al_r[31:0] = in_6
endmodule

module PC (
  input  in_1,
  input  in_2,
  input  [31:0] in_3,
  output [31:0] out_4
);

  wire [31:0] register_1_q, subtractor_1_out;

  Subtractor #(.width(32)) subtractor_1 (.a(in_3), .b(32'h3000), .out(subtractor_1_out));  // open: bin, bout
  Register #(.width(32)) register_1 (.D(subtractor_1_out), .Q(register_1_q), .clk(in_1), .clr(in_2));  // open: en
  Adder #(.width(32)) adder_1 (.a(register_1_q), .b(32'h3000), .out(out_4));  // open: cin, cout

  // Other names for the same wires on the sheet: clk = in_1; PC[31:0] = out_4; PC_prime[31:0] = in_3; reset = in_2
endmodule
