// Logisim project CRC.circ as structural Verilog: 2 circuits, main circuit CRC
module CRC (
  input  [7:0] in_1,
  input  [3:0] in_2,
  output [10:0] out_3
);

  wire [2:0] suan_1_out_6, suan_2_out_6, suan_3_out_6, suan_4_out_6, suan_5_out_6, suan_6_out_6, suan_7_out_6;

  suan suan_1 (.in_1(in_1[4]), .in_2(in_1[5]), .in_3(in_1[6]), .in_4(in_1[7]), .in_5(in_2), .out_6(suan_1_out_6));
  suan suan_2 (
    .in_1(in_1[3]), .in_2(suan_1_out_6[0]), .in_3(suan_1_out_6[1]), .in_4(suan_1_out_6[2]), .in_5(in_2),
    .out_6(suan_2_out_6));
  suan suan_3 (
    .in_1(in_1[2]), .in_2(suan_2_out_6[0]), .in_3(suan_2_out_6[1]), .in_4(suan_2_out_6[2]), .in_5(in_2),
    .out_6(suan_3_out_6));
  suan suan_4 (
    .in_1(in_1[1]), .in_2(suan_3_out_6[0]), .in_3(suan_3_out_6[1]), .in_4(suan_3_out_6[2]), .in_5(in_2),
    .out_6(suan_4_out_6));
  suan suan_5 (
    .in_1(in_1[0]), .in_2(suan_4_out_6[0]), .in_3(suan_4_out_6[1]), .in_4(suan_4_out_6[2]), .in_5(in_2),
    .out_6(suan_5_out_6));
  suan suan_6 (
    .in_1(1'b0), .in_2(suan_5_out_6[0]), .in_3(suan_5_out_6[1]), .in_4(suan_5_out_6[2]), .in_5(in_2),
    .out_6(suan_6_out_6));
  suan suan_7 (
    .in_1(1'b0), .in_2(suan_6_out_6[0]), .in_3(suan_6_out_6[1]), .in_4(suan_6_out_6[2]), .in_5(in_2),
    .out_6(suan_7_out_6));
  suan suan_8 (
    .in_1(1'b0), .in_2(suan_7_out_6[0]), .in_3(suan_7_out_6[1]), .in_4(suan_7_out_6[2]), .in_5(in_2),
    .out_6(out_3[2:0]));

  assign out_3[10:3] = in_1;

  // Other names for the same wires on the sheet: B[3:0] = in_2; A[7:0] = in_1; A0 = in_1[0]; A1 = in_1[1];
  //   A2 = in_1[2]; A3 = in_1[3]; A4 = in_1[4]; A5 = in_1[5]; A6 = in_1[6]; A7 = in_1[7]
endmodule

module suan (
  input  in_1,
  input  in_2,
  input  in_3,
  input  in_4,
  input  [3:0] in_5,
  output [2:0] out_6
);

  wire [3:0] xor_1_out;
  wire [3:3] multiplexer_1_out;

  assign xor_1_out = {in_4, in_3, in_2, in_1} ^ in_5;  // XOR_Gate xor_1, 4 bits wide
  Multiplexer #(.width(4)) multiplexer_1 (
    .in0({in_4, in_3, in_2, in_1}), .in1(xor_1_out), .out({multiplexer_1_out[3], out_6}), .sel(in_4));  // open: en

  // Other names for the same wires on the sheet: A_prime[3:0] = {in_4, in_3, in_2, in_1}; 首位 = in_4
endmodule
