// Logisim project GRF.circ as structural Verilog: 1 circuit, main circuit grf
module grf (
  input  in_1,
  input  in_2,
  input  in_3,
  input  [4:0] in_4,
  input  [4:0] in_5,
  input  [4:0] in_6,
  input  [31:0] in_7,
  output [31:0] out_8,
  output [31:0] out_9
);

  wire [31:0] in2, in3, in4, in5, in6, in7, in8, in9, in10, in11, in12, in13, in14, in15, in16, in17, in18,
       in19, in20, in21, in22, in23, in24, in25, in26, in27, in28, in29, in30, in31, in32, out1, out2, out3,
       out4, out5, out6, out7, out8, out9, out10, out11, out12, out13, out14, out15, out16, out17, out18,
       out19, out20, out21, out22, out23, out24, out25, out26, out27, out28, out29, out30, out31, out32;

  Demultiplexer #(.select(5), .width(32), .tristate("true")) demultiplexer_1 (
    .out1(in2), .out2(in3), .out3(in4), .out4(in5), .out5(in6), .out6(in7), .out7(in8), .out8(in9),
    .out9(in10), .out10(in11), .out11(in12), .out12(in13), .out13(in14), .out14(in15), .out15(in16),
    .out16(in17), .out17(in18), .out18(in19), .out19(in20), .out20(in21), .out21(in22), .out22(in23),
    .out23(in24), .out24(in25), .out25(in26), .out26(in27), .out27(in28), .out28(in29), .out29(in30),
    .out30(in31), .out31(in32), .in(in_7), .sel(in_6));  // open: out0, en
  Multiplexer #(.select(5), .width(32)) multiplexer_1 (
    .in0(out1), .in1(out2), .in2(out3), .in3(out4), .in4(out5), .in5(out6), .in6(out7), .in7(out8),
    .in8(out9), .in9(out10), .in10(out11), .in11(out12), .in12(out13), .in13(out14), .in14(out15),
    .in15(out16), .in16(out17), .in17(out18), .in18(out19), .in19(out20), .in20(out21), .in21(out22),
    .in22(out23), .in23(out24), .in24(out25), .in25(out26), .in26(out27), .in27(out28), .in28(out29),
    .in29(out30), .in30(out31), .in31(out32), .out(out_8), .sel(in_4));  // open: en
  Register #(.width(32)) register_1 (.D({32{1'b0}}), .en(in_3), .Q(out1), .clk(in_1), .clr(in_2));
  Register #(.width(32)) register_2 (.D(in9), .en(in_3), .Q(out9), .clk(in_1), .clr(in_2));
  Register #(.width(32)) register_3 (.D(in17), .en(in_3), .Q(out17), .clk(in_1), .clr(in_2));
  Register #(.width(32)) register_4 (.D(in25), .en(in_3), .Q(out25), .clk(in_1), .clr(in_2));
  Register #(.width(32)) register_5 (.D(in2), .en(in_3), .Q(out2), .clk(in_1), .clr(in_2));
  Register #(.width(32)) register_6 (.D(in10), .en(in_3), .Q(out10), .clk(in_1), .clr(in_2));
  Register #(.width(32)) register_7 (.D(in18), .en(in_3), .Q(out18), .clk(in_1), .clr(in_2));
  Register #(.width(32)) register_8 (.D(in26), .en(in_3), .Q(out26), .clk(in_1), .clr(in_2));
  Register #(.width(32)) register_9 (.D(in3), .en(in_3), .Q(out3), .clk(in_1), .clr(in_2));
  Register #(.width(32)) register_10 (.D(in11), .en(in_3), .Q(out11), .clk(in_1), .clr(in_2));
  Register #(.width(32)) register_11 (.D(in19), .en(in_3), .Q(out19), .clk(in_1), .clr(in_2));
  Register #(.width(32)) register_12 (.D(in27), .en(in_3), .Q(out27), .clk(in_1), .clr(in_2));
  Multiplexer #(.select(5), .width(32)) multiplexer_2 (
    .in0(out1), .in1(out2), .in2(out3), .in3(out4), .in4(out5), .in5(out6), .in6(out7), .in7(out8),
    .in8(out9), .in9(out10), .in10(out11), .in11(out12), .in12(out13), .in13(out14), .in14(out15),
    .in15(out16), .in16(out17), .in17(out18), .in18(out19), .in19(out20), .in20(out21), .in21(out22),
    .in22(out23), .in23(out24), .in24(out25), .in25(out26), .in26(out27), .in27(out28), .in28(out29),
    .in29(out30), .in30(out31), .in31(out32), .out(out_9), .sel(in_5));  // open: en
  Register #(.width(32)) register_13 (.D(in4), .en(in_3), .Q(out4), .clk(in_1), .clr(in_2));
  Register #(.width(32)) register_14 (.D(in12), .en(in_3), .Q(out12), .clk(in_1), .clr(in_2));
  Register #(.width(32)) register_15 (.D(in20), .en(in_3), .Q(out20), .clk(in_1), .clr(in_2));
  Register #(.width(32)) register_16 (.D(in28), .en(in_3), .Q(out28), .clk(in_1), .clr(in_2));
  Register #(.width(32)) register_17 (.D(in5), .en(in_3), .Q(out5), .clk(in_1), .clr(in_2));
  Register #(.width(32)) register_18 (.D(in13), .en(in_3), .Q(out13), .clk(in_1), .clr(in_2));
  Register #(.width(32)) register_19 (.D(in21), .en(in_3), .Q(out21), .clk(in_1), .clr(in_2));
  Register #(.width(32)) register_20 (.D(in29), .en(in_3), .Q(out29), .clk(in_1), .clr(in_2));
  Register #(.width(32)) register_21 (.D(in6), .en(in_3), .Q(out6), .clk(in_1), .clr(in_2));
  Register #(.width(32)) register_22 (.D(in14), .en(in_3), .Q(out14), .clk(in_1), .clr(in_2));
  Register #(.width(32)) register_23 (.D(in22), .en(in_3), .Q(out22), .clk(in_1), .clr(in_2));
  Register #(.width(32)) register_24 (.D(in30), .en(in_3), .Q(out30), .clk(in_1), .clr(in_2));
  Register #(.width(32)) register_25 (.D(in7), .en(in_3), .Q(out7), .clk(in_1), .clr(in_2));
  Register #(.width(32)) register_26 (.D(in15), .en(in_3), .Q(out15), .clk(in_1), .clr(in_2));
  Register #(.width(32)) register_27 (.D(in23), .en(in_3), .Q(out23), .clk(in_1), .clr(in_2));
  Register #(.width(32)) register_28 (.D(in31), .en(in_3), .Q(out31), .clk(in_1), .clr(in_2));
  Register #(.width(32)) register_29 (.D(in8), .en(in_3), .Q(out8), .clk(in_1), .clr(in_2));
  Register #(.width(32)) register_30 (.D(in16), .en(in_3), .Q(out16), .clk(in_1), .clr(in_2));
  Register #(.width(32)) register_31 (.D(in24), .en(in_3), .Q(out24), .clk(in_1), .clr(in_2));
  Register #(.width(32)) register_32 (.D(in32), .en(in_3), .Q(out32), .clk(in_1), .clr(in_2));

  // Other names for the same wires on the sheet: A1[4:0] = in_4; A2[4:0] = in_5; A3[4:0] = in_6; clk = in_1;
  //   RD1[31:0] = out_8; RD2[31:0] = out_9; reset = in_2; WD[31:0] = in_7; we = in_3
endmodule
