// Logisim project fibonacci_1.circ as structural Verilog: 1 circuit, main circuit main
module main (
  input  [2:0] in_1,
  output [3:0] out_2
);

  wire clock, comparator_1_lt, comparator_2_gt, enable, judge;
  wire [3:0] adder_1_out, bit_extender_1_out, counter_1_q, multiplexer_1_out, register_1_q, register_2_q;

  Clock clock_1 (.out(clock));
  Register #(.width(4)) register_1 (.D(multiplexer_1_out), .en(enable), .Q(register_1_q), .clk(clock), .clr(1'b0));
  Multiplexer #(.width(4)) multiplexer_1 (
    .in0(4'b0001), .in1(register_2_q), .out(multiplexer_1_out), .sel(judge));  // open: en
  Counter #(.width(4), .max('hf), .ongoal("stay")) counter_1 (
    .Q(counter_1_q), .clk(clock), .clr(1'b0));  // open: load, D, count, carry
  Adder #(.width(4)) adder_1 (.a(register_1_q), .b(register_2_q), .out(adder_1_out));  // open: cin, cout
  assign bit_extender_1_out = {{1{1'b0}}, in_1};  // Bit_Extender bit_extender_1
  Register #(.width(4)) register_2 (.D(adder_1_out), .en(enable), .Q(register_2_q), .clk(clock), .clr(1'b0));
  Comparator #(.width(4), .mode("unsigned")) comparator_1 (
    .a(bit_extender_1_out), .b(counter_1_q), .lt(comparator_1_lt));  // open: gt, eq
  Comparator #(.width(4), .mode("unsigned")) comparator_2 (
    .a(4'b0001), .b(counter_1_q), .gt(comparator_2_gt));  // open: eq, lt
  not not_1 (judge, comparator_2_gt);
  not not_2 (enable, comparator_1_lt);
  Multiplexer #(.width(4)) multiplexer_2 (
    .in0(4'b0000), .in1(register_2_q), .out(out_2), .sel(comparator_1_lt));  // open: en
endmodule
