// Logisim project fibonacci_2.circ as structural Verilog: 4 circuits, main circuit matrix_multi
module main (
  input  [31:0] in_1,
  output [31:0] out_2
);

  matrix_pow matrix_pow_1 (.in_1(in_1), .out_3(out_2));  // open: in_2
endmodule

module matrix_multi (
  input  [31:0] in_1,
  input  [31:0] in_2,
  input  [31:0] in_3,
  input  [31:0] in_4,
  input  [31:0] in_5,
  input  [31:0] in_6,
  input  [31:0] in_7,
  input  [31:0] in_8,
  output [31:0] out_9,
  output [31:0] out_10,
  output [31:0] out_11,
  output [31:0] out_12
);

  wire [31:0] multiplier_1_out, multiplier_2_out, multiplier_3_out, multiplier_4_out, multiplier_5_out,
       multiplier_6_out, multiplier_7_out, multiplier_8_out;

  Multiplier #(.width(32)) multiplier_1 (.a(in_1), .b(in_5), .out(multiplier_1_out));  // open: cin, cout
  Multiplier #(.width(32)) multiplier_2 (.a(in_2), .b(in_7), .out(multiplier_2_out));  // open: cin, cout
  Multiplier #(.width(32)) multiplier_3 (.a(in_1), .b(in_6), .out(multiplier_3_out));  // open: cin, cout
  Multiplier #(.width(32)) multiplier_4 (.a(in_2), .b(in_8), .out(multiplier_4_out));  // open: cin, cout
  Multiplier #(.width(32)) multiplier_5 (.a(in_3), .b(in_5), .out(multiplier_5_out));  // open: cin, cout
  Multiplier #(.width(32)) multiplier_6 (.a(in_4), .b(in_7), .out(multiplier_6_out));  // open: cin, cout
  Multiplier #(.width(32)) multiplier_7 (.a(in_3), .b(in_6), .out(multiplier_7_out));  // open: cin, cout
  Multiplier #(.width(32)) multiplier_8 (.a(in_4), .b(in_8), .out(multiplier_8_out));  // open: cin, cout
  Adder #(.width(32)) adder_1 (.a(multiplier_1_out), .b(multiplier_2_out), .out(out_9));  // open: cin, cout
  Adder #(.width(32)) adder_2 (.a(multiplier_3_out), .b(multiplier_4_out), .out(out_10));  // open: cin, cout
  Adder #(.width(32)) adder_3 (.a(multiplier_5_out), .b(multiplier_6_out), .out(out_11));  // open: cin, cout
  Adder #(.width(32)) adder_4 (.a(multiplier_7_out), .b(multiplier_8_out), .out(out_12));  // open: cin, cout

  // Other names for the same wires on the sheet: a00[31:0] = in_1; a01[31:0] = in_2; a10[31:0] = in_3;
  //   a11[31:0] = in_4; b00[31:0] = in_5; b01[31:0] = in_6; b10[31:0] = in_7; b11[31:0] = in_8
endmodule

module matrix_MUX (
  input  [31:0] in_1,
  input  [31:0] in_2,
  input  [31:0] in_3,
  input  [31:0] in_4,
  input  [31:0] in_5,
  input  [31:0] in_6,
  input  [31:0] in_7,
  input  [31:0] in_8,
  input  in_9,
  output [31:0] out_10,
  output [31:0] out_11,
  output [31:0] out_12,
  output [31:0] out_13
);

  Multiplexer #(.width(32)) multiplexer_1 (.in0(in_1), .in1(in_5), .out(out_10), .sel(in_9));  // open: en
  Multiplexer #(.width(32)) multiplexer_2 (.in0(in_2), .in1(in_6), .out(out_11), .sel(in_9));  // open: en
  Multiplexer #(.width(32)) multiplexer_3 (.in0(in_3), .in1(in_7), .out(out_12), .sel(in_9));  // open: en
  Multiplexer #(.width(32)) multiplexer_4 (.in0(in_4), .in1(in_8), .out(out_13), .sel(in_9));  // open: en

  // Other names for the same wires on the sheet: a00[31:0] = in_1; a01[31:0] = in_2; a10[31:0] = in_3;
  //   a11[31:0] = in_4; b00[31:0] = in_5; b01[31:0] = in_6; b10[31:0] = in_7; b11[31:0] = in_8
endmodule

module matrix_pow (
  input  [31:0] in_1,
  input  in_2,
  output [31:0] out_3
);

  wire clock, comparator_1_eq, enable, judge_1, judge_1or0, judge_out;
  wire [31:0] a00, a01, a10, a11, multi_2_out_9, multi_2_out_10, multi_2_out_11, multi_2_out_12, multi_out_9,
       multi_out_10, multi_out_11, multi_out_12, multiplexer_1_out, MUX_2_out_10, MUX_2_out_11, MUX_2_out_12,
       MUX_2_out_13, MUX_3_out_10, MUX_3_out_11, MUX_3_out_12, MUX_3_out_13, MUX_out_10, MUX_out_11,
       MUX_out_12, MUX_out_13, register_1_q, register_6_q, register_7_q, register_8_q, register_9_q,
       shifter_1_out;

  Clock clock_1 (.out(clock));
  not not_1 (enable, judge_out);
  Counter #(.width(1), .max('h1), .ongoal("stay")) counter_1 (
    .Q(judge_1), .clk(clock), .clr(in_2));  // open: load, D, count, carry
  Shifter #(.width(32), .shift("lr")) shifter_1 (.in(register_1_q), .\dist (5'b00001), .out(shifter_1_out));
  matrix_multi multi (
    .in_1(a00), .in_2(a01), .in_3(a10), .in_4(a11), .in_5(a00), .in_6(a01), .in_7(a10), .in_8(a11),
    .out_9(multi_out_9), .out_10(multi_out_10), .out_11(multi_out_11), .out_12(multi_out_12));
  Multiplexer #(.width(32)) multiplexer_1 (
    .in0(in_1), .in1(shifter_1_out), .out(multiplexer_1_out), .sel(judge_1));  // open: en
  matrix_MUX MUX (
    .in_1(32'h1), .in_2(32'h1), .in_3(32'h1), .in_4({32{1'b0}}), .in_5(multi_out_9), .in_6(multi_out_10),
    .in_7(multi_out_11), .in_8(multi_out_12), .in_9(judge_1), .out_10(MUX_out_10), .out_11(MUX_out_11),
    .out_12(MUX_out_12), .out_13(MUX_out_13));
  Register #(.width(32)) register_1 (.D(multiplexer_1_out), .Q(register_1_q), .clk(clock));  // open: en, clr
  Comparator #(.width(32)) comparator_1 (.a(register_1_q), .b({32{1'b0}}), .eq(comparator_1_eq));  // open: gt, lt
  Bit_Extender #(.in_width(32), .out_width(1)) bit_extender_1 (.in(register_1_q), .out(judge_1or0));
  Register #(.width(32)) register_2 (.D(MUX_out_10), .en(enable), .Q(a00), .clk(clock), .clr(in_2));
  Register #(.width(32)) register_3 (.D(MUX_out_11), .en(enable), .Q(a01), .clk(clock), .clr(in_2));
  Register #(.width(32)) register_4 (.D(MUX_out_12), .en(enable), .Q(a10), .clk(clock), .clr(in_2));
  Register #(.width(32)) register_5 (.D(MUX_out_13), .en(enable), .Q(a11), .clk(clock), .clr(in_2));
  Multiplexer multiplexer_2 (.in0(1'b0), .in1(comparator_1_eq), .out(judge_out), .sel(judge_1));  // open: en
  Multiplexer #(.width(32)) multiplexer_3 (
    .in0({32{1'b0}}), .in1(register_7_q), .out(out_3), .sel(judge_out));  // open: en
  matrix_MUX MUX_2 (
    .in_1(32'h1), .in_2({32{1'b0}}), .in_3({32{1'b0}}), .in_4(32'h1), .in_5(a00), .in_6(a01), .in_7(a10),
    .in_8(a11), .in_9(judge_1or0), .out_10(MUX_2_out_10), .out_11(MUX_2_out_11), .out_12(MUX_2_out_12),
    .out_13(MUX_2_out_13));
  matrix_multi multi_2 (
    .in_1(MUX_2_out_10), .in_2(MUX_2_out_11), .in_3(MUX_2_out_12), .in_4(MUX_2_out_13), .in_5(register_6_q),
    .in_6(register_7_q), .in_7(register_8_q), .in_8(register_9_q), .out_9(multi_2_out_9),
    .out_10(multi_2_out_10), .out_11(multi_2_out_11), .out_12(multi_2_out_12));
  matrix_MUX MUX_3 (
    .in_1(32'h1), .in_2({32{1'b0}}), .in_3({32{1'b0}}), .in_4(32'h1), .in_5(multi_2_out_9),
    .in_6(multi_2_out_10), .in_7(multi_2_out_11), .in_8(multi_2_out_12), .in_9(judge_1),
    .out_10(MUX_3_out_10), .out_11(MUX_3_out_11), .out_12(MUX_3_out_12), .out_13(MUX_3_out_13));
  Register #(.width(32)) register_6 (.D(MUX_3_out_10), .en(enable), .Q(register_6_q), .clk(clock), .clr(in_2));
  Register #(.width(32)) register_7 (.D(MUX_3_out_11), .en(enable), .Q(register_7_q), .clk(clock), .clr(in_2));
  Register #(.width(32)) register_8 (.D(MUX_3_out_12), .en(enable), .Q(register_8_q), .clk(clock), .clr(in_2));
  Register #(.width(32)) register_9 (.D(MUX_3_out_13), .en(enable), .Q(register_9_q), .clk(clock), .clr(in_2));

  // Other names for the same wires on the sheet: clr = in_2
endmodule
