// Logisim project fsm.circ as structural Verilog: 3 circuits, main circuit fsm
module fsm (
  input  in_1,
  input  [1:0] in_2,
  output out_3
);

  wire clk;
  wire [1:0] multiplexer_1_out, next_state_1_out_3, State;

  Clock clock_1 (.out(clk));
  suan suan_1 (.in_1(State), .in_2(in_2), .O(out_3));
  // Probe on State
  Next_State next_state_1 (.in_1(State), .in_2(in_2), .out_3(next_state_1_out_3));
  // Probe on multiplexer_1_out
  Multiplexer #(.width(2)) multiplexer_1 (
    .in0(next_state_1_out_3), .in1(2'b00), .out(multiplexer_1_out), .sel(in_1));  // open: en
  Register #(.width(2)) register_1 (.D(multiplexer_1_out), .Q(State), .clk(clk));  // open: en, clr

  // Other names for the same wires on the sheet: clr = in_1; In[1:0] = in_2
endmodule

module Next_State (
  input  [1:0] in_1,
  input  [1:0] in_2,
  output [1:0] out_3
);

  wire and_2_out, and_3_out, not_1_out, not_2_out, not_3_out, not_4_out, not_5_out, not_6_out;

  not not_1 (not_1_out, in_1[1]);
  and and_1 (out_3[1], not_1_out, in_1[0], not_2_out);
  not not_2 (not_2_out, in_2[0]);
  not not_3 (not_3_out, in_1[1]);
  and and_2 (and_2_out, not_3_out, not_4_out, in_2[0]);
  not not_4 (not_4_out, in_2[1]);
  not not_5 (not_5_out, in_1[0]);
  not not_6 (not_6_out, in_2[1]);
  and and_3 (and_3_out, not_5_out, not_6_out, in_2[0]);
  or or_1 (out_3[0], and_2_out, and_3_out);

  // Other names for the same wires on the sheet: S0 = in_1[0]; S1 = in_1[1]; I0 = in_2[0]; I1 = in_2[1];
  //   NS0 = out_3[0]; NS1 = out_3[1]
endmodule

module suan (
  input  [1:0] in_1,
  input  [1:0] in_2,
  output O
);

  wire not_1_out, not_2_out;

  and and_1 (O, in_1[1], not_1_out, not_2_out);
  not not_1 (not_1_out, in_1[0]);
  not not_2 (not_2_out, in_2[0]);

  // Other names for the same wires on the sheet: S0 = in_1[0]; S1 = in_1[1]; I1 = in_2[1]
endmodule
