// Logisim project ftoi.circ as structural Verilog: 4 circuits, main circuit ftoi
module ftoi (
  input  [15:0] in_1,
  output [31:0] out_2
);

  wire comparator_1_eq, comparator_2_eq, isNor, or_1_out;
  wire [31:0] ans, multiplexer_1_out, negator_1_out;

  // Probe on ans
  suan suan_1 (.in_1(in_1), .out_2(ans));
  Comparator #(.width(5)) comparator_1 (.a(in_1[14:10]), .b({5{1'b0}}), .eq(comparator_1_eq));  // open: gt, lt
  or or_1 (or_1_out, comparator_1_eq, comparator_2_eq);
  Comparator #(.width(5)) comparator_2 (.a(in_1[14:10]), .b({5{1'b1}}), .eq(comparator_2_eq));  // open: gt, lt
  not not_1 (isNor, or_1_out);
  Negator #(.width(32)) negator_1 (.in(ans), .out(negator_1_out));
  Multiplexer #(.width(32)) multiplexer_1 (
    .in0(ans), .in1(negator_1_out), .out(multiplexer_1_out), .sel(in_1[15]));  // open: en
  Multiplexer #(.width(32)) multiplexer_2 (
    .in0({32{1'b0}}), .in1(multiplexer_1_out), .out(out_2), .sel(isNor));  // open: en

  // Other names for the same wires on the sheet: input[15:0] = in_1; is_minus = in_1[15]
endmodule

module suan (
  input  [15:0] in_1,
  output [31:0] out_2
);

  wire isMul;
  wire [4:0] E, subtractor_1_out;
  wire [31:0] _2_E, fra_E;

  _2_E u_2_e_1 (.in_1(E), .out_2(_2_E));
  fra fra_1 (.in_1(in_1[9:0]), .in_2(_2_E), .out_3(fra_E));
  // Probe on _2_E
  Multiplexer #(.width(32)) multiplexer_1 (.in0(fra_E), .in1({32{1'b0}}), .out(out_2), .sel(isMul));  // open: en
  Subtractor #(.width(5)) subtractor_1 (
    .a(in_1[14:10]), .b(5'b01111), .out(subtractor_1_out), .bout(isMul));  // open: bin
  // Probe on fra_E
  Multiplexer #(.width(5)) multiplexer_2 (.in0(subtractor_1_out), .in1({5{1'b0}}), .out(E), .sel(isMul));  // open: en

  // Other names for the same wires on the sheet: fra[9:0] = in_1[9:0]; exp[4:0] = in_1[14:10]; sign = in_1[15]
endmodule

module _2_E (
  input  [4:0] in_1,
  output [31:0] out_2
);

  wire [31:0] multiplexer_1_out, multiplexer_2_out, multiplexer_3_out, multiplexer_4_out, multiplexer_5_out,
       multiplier_1_out, multiplier_2_out, multiplier_3_out;

  Multiplexer #(.width(32)) multiplexer_1 (
    .in0(32'h1), .in1(32'h2), .out(multiplexer_1_out), .sel(in_1[0]));  // open: en
  Multiplexer #(.width(32)) multiplexer_2 (
    .in0(32'h1), .in1(32'h4), .out(multiplexer_2_out), .sel(in_1[1]));  // open: en
  Multiplexer #(.width(32)) multiplexer_3 (
    .in0(32'h1), .in1(32'h10), .out(multiplexer_3_out), .sel(in_1[2]));  // open: en
  Multiplexer #(.width(32)) multiplexer_4 (
    .in0(32'h1), .in1(32'h100), .out(multiplexer_4_out), .sel(in_1[3]));  // open: en
  Multiplexer #(.width(32)) multiplexer_5 (
    .in0(32'h1), .in1(32'h10000), .out(multiplexer_5_out), .sel(in_1[4]));  // open: en
  Multiplier #(.width(32)) multiplier_1 (
    .a(multiplexer_1_out), .b(multiplexer_2_out), .out(multiplier_1_out));  // open: cin, cout
  Multiplier #(.width(32)) multiplier_2 (
    .a(multiplexer_3_out), .b(multiplexer_4_out), .out(multiplier_2_out));  // open: cin, cout
  Multiplier #(.width(32)) multiplier_3 (
    .a(multiplier_2_out), .b(multiplexer_5_out), .out(multiplier_3_out));  // open: cin, cout
  Multiplier #(.width(32)) multiplier_4 (.a(multiplier_1_out), .b(multiplier_3_out), .out(out_2));  // open: cin, cout

  // Other names for the same wires on the sheet: _1 = in_1[0]; _2 = in_1[1]; _3 = in_1[2]; _4 = in_1[3]; _5 = in_1[4]
endmodule

module fra (
  input  [9:0] in_1,
  input  [31:0] in_2,
  output [31:0] out_3
);

  wire [31:0] adder_1_out, adder_2_out, adder_3_out, adder_4_out, adder_5_out, adder_6_out, adder_7_out,
       adder_8_out, adder_9_out, divider_1_out, divider_2_out, divider_3_out, divider_4_out, divider_5_out,
       divider_6_out, divider_7_out, divider_8_out, divider_9_out, divider_10_out, multiplexer_1_out,
       multiplexer_2_out, multiplexer_3_out, multiplexer_4_out, multiplexer_5_out, multiplexer_6_out,
       multiplexer_7_out, multiplexer_8_out, multiplexer_9_out, multiplexer_10_out;

  Divider #(.width(32)) divider_1 (.a(in_2), .b(32'h2), .out(divider_1_out));  // open: upper, rem
  Divider #(.width(32)) divider_2 (.a(in_2), .b(32'h4), .out(divider_2_out));  // open: upper, rem
  Divider #(.width(32)) divider_3 (.a(in_2), .b(32'h8), .out(divider_3_out));  // open: upper, rem
  Divider #(.width(32)) divider_4 (.a(in_2), .b(32'h10), .out(divider_4_out));  // open: upper, rem
  Divider #(.width(32)) divider_5 (.a(in_2), .b(32'h20), .out(divider_5_out));  // open: upper, rem
  Divider #(.width(32)) divider_6 (.a(in_2), .b(32'h40), .out(divider_6_out));  // open: upper, rem
  Divider #(.width(32)) divider_7 (.a(in_2), .b(32'h80), .out(divider_7_out));  // open: upper, rem
  Divider #(.width(32)) divider_8 (.a(in_2), .b(32'h100), .out(divider_8_out));  // open: upper, rem
  Divider #(.width(32)) divider_9 (.a(in_2), .b(32'h200), .out(divider_9_out));  // open: upper, rem
  Divider #(.width(32)) divider_10 (.a(in_2), .b(32'h400), .out(divider_10_out));  // open: upper, rem
  Multiplexer #(.width(32)) multiplexer_1 (
    .in0({32{1'b0}}), .in1(divider_1_out), .out(multiplexer_1_out), .sel(in_1[9]));  // open: en
  Multiplexer #(.width(32)) multiplexer_2 (
    .in0({32{1'b0}}), .in1(divider_2_out), .out(multiplexer_2_out), .sel(in_1[8]));  // open: en
  Multiplexer #(.width(32)) multiplexer_3 (
    .in0({32{1'b0}}), .in1(divider_3_out), .out(multiplexer_3_out), .sel(in_1[7]));  // open: en
  Multiplexer #(.width(32)) multiplexer_4 (
    .in0({32{1'b0}}), .in1(divider_4_out), .out(multiplexer_4_out), .sel(in_1[6]));  // open: en
  Multiplexer #(.width(32)) multiplexer_5 (
    .in0({32{1'b0}}), .in1(divider_5_out), .out(multiplexer_5_out), .sel(in_1[5]));  // open: en
  Multiplexer #(.width(32)) multiplexer_6 (
    .in0({32{1'b0}}), .in1(divider_6_out), .out(multiplexer_6_out), .sel(in_1[4]));  // open: en
  Multiplexer #(.width(32)) multiplexer_7 (
    .in0({32{1'b0}}), .in1(divider_7_out), .out(multiplexer_7_out), .sel(in_1[3]));  // open: en
  Multiplexer #(.width(32)) multiplexer_8 (
    .in0({32{1'b0}}), .in1(divider_8_out), .out(multiplexer_8_out), .sel(in_1[2]));  // open: en
  Multiplexer #(.width(32)) multiplexer_9 (
    .in0({32{1'b0}}), .in1(divider_9_out), .out(multiplexer_9_out), .sel(in_1[1]));  // open: en
  Multiplexer #(.width(32)) multiplexer_10 (
    .in0({32{1'b0}}), .in1(divider_10_out), .out(multiplexer_10_out), .sel(in_1[0]));  // open: en
  Adder #(.width(32)) adder_1 (.a(multiplexer_1_out), .b(multiplexer_2_out), .out(adder_1_out));  // open: cin, cout
  Adder #(.width(32)) adder_2 (.a(multiplexer_3_out), .b(multiplexer_4_out), .out(adder_2_out));  // open: cin, cout
  Adder #(.width(32)) adder_3 (.a(multiplexer_5_out), .b(multiplexer_6_out), .out(adder_3_out));  // open: cin, cout
  Adder #(.width(32)) adder_4 (.a(multiplexer_7_out), .b(multiplexer_8_out), .out(adder_4_out));  // open: cin, cout
  Adder #(.width(32)) adder_5 (.a(multiplexer_9_out), .b(multiplexer_10_out), .out(adder_5_out));  // open: cin, cout
  Adder #(.width(32)) adder_6 (.a(adder_1_out), .b(adder_2_out), .out(adder_6_out));  // open: cin, cout
  Adder #(.width(32)) adder_7 (.a(adder_3_out), .b(adder_4_out), .out(adder_7_out));  // open: cin, cout
  Adder #(.width(32)) adder_8 (.a(adder_7_out), .b(adder_5_out), .out(adder_8_out));  // open: cin, cout
  Adder #(.width(32)) adder_9 (.a(adder_6_out), .b(adder_8_out), .out(adder_9_out));  // open: cin, cout
  Adder #(.width(32)) adder_10 (.a(adder_9_out), .b(in_2), .out(out_3));  // open: cin, cout

  // Other names for the same wires on the sheet: _2_E[31:0] = in_2; _10 = in_1[0]; _9 = in_1[1]; _8 = in_1[2];
  //   _7 = in_1[3]; _6 = in_1[4]; _5 = in_1[5]; _4 = in_1[6]; _3 = in_1[7]; _2 = in_1[8]; _1 = in_1[9]
endmodule
