// Logisim project sort.circ as structural Verilog: 4 circuits, main circuit 1bit_swap
module _1bit_swap (
  input  l1,
  input  l2,
  input  S,
  output O1,
  output O2
);

  wire and_1_out, and_2_out, and_3_out, and_4_out, not_1_out;

  not not_1 (not_1_out, S);
  and and_1 (and_1_out, not_1_out, l1);
  and and_2 (and_2_out, l1, S);
  and and_3 (and_3_out, S, l2);
  and and_4 (and_4_out, l2, not_1_out);
  or or_1 (O1, and_1_out, and_3_out);
  or or_2 (O2, and_2_out, and_4_out);
endmodule

module _4bit_swap (
  input  [3:0] in_1,
  input  [3:0] in_2,
  input  in_3,
  output [3:0] out_4,
  output [3:0] out_5
);

  _1bit_swap u_1bit_swap_1 (.l1(in_1[0]), .l2(in_2[0]), .S(in_3), .O1(out_4[0]), .O2(out_5[0]));
  _1bit_swap u_1bit_swap_2 (.l1(in_1[1]), .l2(in_2[1]), .S(in_3), .O1(out_4[1]), .O2(out_5[1]));
  _1bit_swap u_1bit_swap_3 (.l1(in_1[2]), .l2(in_2[2]), .S(in_3), .O1(out_4[2]), .O2(out_5[2]));
  _1bit_swap u_1bit_swap_4 (.l1(in_1[3]), .l2(in_2[3]), .S(in_3), .O1(out_4[3]), .O2(out_5[3]));

  // Other names for the same wires on the sheet: _10 = in_1[0]; _11 = in_1[1]; _12 = in_1[2]; _13 = in_1[3];
  //   _20 = in_2[0]; _21 = in_2[1]; _22 = in_2[2]; _23 = in_2[3]; n10 = out_4[0]; n11 = out_4[1]; n12 = out_4[2];
  //   n13 = out_4[3]; n20 = out_5[0]; n21 = out_5[1]; n22 = out_5[2]; n23 = out_5[3]; S = in_3
endmodule

module twotwoswap (
  input  [3:0] in_1,
  input  [3:0] in_2,
  output [3:0] out_3,
  output [3:0] out_4
);

  wire comparator_1_gt;

  Comparator #(.width(4), .mode("unsigned")) comparator_1 (.a(in_1), .b(in_2), .gt(comparator_1_gt));  // open: eq, lt
  _4bit_swap u_4bit_swap_1 (.in_1(in_1), .in_2(in_2), .in_3(comparator_1_gt), .out_4(out_3), .out_5(out_4));
endmodule

module _4bit_sort (
  input  [3:0] in_1,
  input  [3:0] in_2,
  input  [3:0] in_3,
  input  [3:0] in_4,
  output [3:0] out_5,
  output [3:0] out_6,
  output [3:0] out_7,
  output [3:0] out_8
);

  wire [3:0] twotwoswap_1_out_3, twotwoswap_1_out_4, twotwoswap_2_out_3, twotwoswap_2_out_4,
       twotwoswap_3_out_3, twotwoswap_4_out_3, twotwoswap_4_out_4, twotwoswap_5_out_3;

  twotwoswap twotwoswap_1 (.in_1(in_1), .in_2(in_2), .out_3(twotwoswap_1_out_3), .out_4(twotwoswap_1_out_4));
  twotwoswap twotwoswap_2 (
    .in_1(twotwoswap_1_out_4), .in_2(in_3), .out_3(twotwoswap_2_out_3), .out_4(twotwoswap_2_out_4));
  twotwoswap twotwoswap_3 (.in_1(twotwoswap_2_out_4), .in_2(in_4), .out_3(twotwoswap_3_out_3), .out_4(out_8));
  twotwoswap twotwoswap_4 (
    .in_1(twotwoswap_1_out_3), .in_2(twotwoswap_2_out_3), .out_3(twotwoswap_4_out_3),
    .out_4(twotwoswap_4_out_4));
  twotwoswap twotwoswap_5 (
    .in_1(twotwoswap_4_out_4), .in_2(twotwoswap_3_out_3), .out_3(twotwoswap_5_out_3), .out_4(out_7));
  twotwoswap twotwoswap_6 (.in_1(twotwoswap_4_out_3), .in_2(twotwoswap_5_out_3), .out_3(out_5), .out_4(out_6));
endmodule
